// Logisim project PD1.circ as structural Verilog: 1 circuit, main circuit main
module main (
  input  [3:0] A,
  input  [3:0] B
);

  wire comparator_1_gt, comparator_2_lt, or_1_out;
  wire [4:0] adder_2_out, ELSE, IF, Y;

  // Probe on A
  // Probe on B
  Comparator #(.width(4), .mode("unsigned")) comparator_1 (
    .a({1'b0, A[2:0]}), .b({A[3], 3'b011}), .gt(comparator_1_gt));  // open: eq, lt
  Comparator #(.width(4), .mode("unsigned")) comparator_2 (
    .a({1'b0, B[2:0]}), .b({B[3], 3'b100}), .lt(comparator_2_lt));  // open: gt, eq
  // Probe on IF
  Adder #(.width(5)) adder_1 (.a({{2{A[3]}}, A[2:0]}), .b(5'b00011), .out(IF));  // open: cin, cout
  // Probe on adder_2_out
  Adder #(.width(5)) adder_2 (.a({{2{B[3]}}, B[2:0]}), .b({{2{B[3]}}, B[2:0]}), .out(adder_2_out));  // open: cin, cout
  // Probe on comparator_1_gt
  or or_1 (or_1_out, comparator_1_gt, comparator_2_lt);
  // Probe on comparator_2_lt
  // Probe on ELSE
  Adder #(.width(5)) adder_3 (.a(adder_2_out), .b(5'b11100), .out(ELSE));  // open: cin, cout
  Multiplexer #(.width(5), .disabled(0), .enable("false")) multiplexer_1 (
    .in0(ELSE), .in1(IF), .out(Y), .sel(or_1_out));
  // Probe on Y

  // Notes on the sheet:
  //   IF
  //   Resultado IF
  //   Resultado ELSE
  //   Solución
endmodule
