// Logisim project PD2.circ as structural Verilog: 1 circuit, main circuit main
module main (
  input  [3:0] in_1,
  input  in_2,
  input  [3:0] in_3
);

  wire CLK, comparator_1_eq, comparator_2_lt, comparator_3_gt, MOSTRAR, not_1_out;
  wire [2:0] CICLO, counter_2_q, Y;
  wire [3:0] A, multiplexer_1_out;

  Clock clock_1 (.out(CLK));
  Comparator #(.width(3), .mode("unsigned")) comparator_1 (
    .a(CICLO), .b(3'b001), .eq(comparator_1_eq));  // open: gt, lt
  Comparator #(.width(4), .mode("unsigned")) comparator_2 (.a(in_1), .b(in_3), .lt(comparator_2_lt));  // open: gt, eq
  not not_1 (not_1_out, CLK);
  Multiplexer #(.width(4), .disabled(0), .enable("false")) multiplexer_1 (
    .in0(4'b0000), .in1(in_1), .out(multiplexer_1_out), .sel(comparator_2_lt));
  Counter #(.width(3), .max('h7)) counter_1 (
    .D(3'b001), .Q(CICLO), .carry(MOSTRAR), .clk(CLK), .clr(in_2));  // open: load, count
  Register #(.width(4)) register_1 (.D(in_1), .en(comparator_1_eq), .Q(A), .clk(not_1_out), .clr(in_2));
  Comparator #(.width(4), .mode("unsigned")) comparator_3 (
    .a(multiplexer_1_out), .b(A), .gt(comparator_3_gt));  // open: eq, lt
  // Probe on CICLO
  // Probe on MOSTRAR
  // Probe on A
  Counter #(.width(3), .max('h7)) counter_2 (
    .D(3'b001), .count(comparator_3_gt), .Q(counter_2_q), .clk(CLK), .clr(in_2));  // open: load, carry
  Multiplexer #(.width(3), .disabled(0), .enable("false")) multiplexer_2 (
    .in0(3'b000), .in1(counter_2_q), .out(Y), .sel(MOSTRAR));
  // Probe on Y

  // Other names for the same wires on the sheet: B[3:0] = in_3; RST = in_2; X[3:0] = in_1

  // Notes on the sheet:
  //   Registrar valor de A
  //   Circuito
  //   Contador de ciclos
  //   Solucion
endmodule
